# Fritzing sketch pow (saved by Fritzing 0.9.0b)
breadboards: 1

parts:
  Raspberry_Pi1 = Raspberry Pi B rev2
  R1 = Resistor [tolerance=±5% resistance=220 package=THT]
  LED1 = LED - 5mm [color="Green (555nm)" package="5 mm [THT]"]
  J1 = Basic Servo
  J2 = Basic Servo
  R2 = Resistor [tolerance=±5% resistance=220 package=THT]
  LED2 = LED - 5mm [color="Infrared (940nm)" package="5 mm [THT]"]

nets:
  GND: Raspberry_Pi1.GND, LED1.cathode, J1.gnd, J1.pulse, J2.gnd
  N1: Raspberry_Pi1.GPIO_17, J2.pulse
  N2: Raspberry_Pi1.GPIO_25, R1.Pin_1
  VCC: Raspberry_Pi1.5V, J1.vcc, J2.vcc, R2.Pin_0, LED2.cathode
  N3: R1.Pin_0, LED1.anode
  N4: R2.Pin_1, LED2.anode
